// Logisim project Circuit.circ as structural Verilog: 1 circuit, main circuit main
module main (
  input  in_1,
  input  in_2,
  input  in_3,
  input  in_4,
  input  in_5,
  input  in_6,
  input  in_7,
  input  in_8,
  input  in_9,
  input  in_10,
  input  in_11,
  input  in_12,
  input  in_13,
  input  in_14,
  input  in_15,
  input  in_16,
  input  in_17,
  input  in_18,
  input  in_19,
  input  in_20,
  input  in_21,
  input  in_22,
  input  in_23,
  input  in_24
);

  wire adder_1_cout, adder_1_out, adder_2_cout, adder_2_out, adder_3_cout, adder_3_out, adder_4_cout,
       adder_4_out, adder_5_cout, adder_5_out, adder_6_cout, adder_6_out, adder_7_cout, adder_7_out,
       adder_8_cout, adder_8_out, adder_9_cout, adder_9_out, adder_10_cout, adder_10_out, adder_11_cout,
       adder_11_out, adder_12_cout, adder_12_out, adder_13_cout, adder_13_out, adder_14_cout, adder_14_out,
       adder_15_cout, adder_15_out, adder_16_cout, adder_16_out, adder_17_cout, adder_17_out, adder_18_cout,
       adder_18_out, adder_19_cout, adder_19_out, adder_20_cout, adder_20_out, adder_21_cout, adder_21_out,
       adder_22_cout, adder_22_out, adder_23_cout, adder_23_out, adder_24_cout, adder_24_out, not_1_out,
       not_2_out, not_3_out, not_4_out, not_5_out, not_6_out, not_7_out, not_8_out, not_9_out, not_10_out,
       not_11_out, not_12_out, not_13_out, not_14_out, not_15_out, not_16_out, not_17_out, not_18_out,
       not_19_out, not_20_out, not_21_out, not_22_out, not_23_out, not_24_out;

  not not_1 (not_1_out, in_1);
  LED led_1 (.in(adder_1_out));
  not not_2 (not_2_out, in_2);
  Adder #(.width(1)) adder_1 (.a(not_1_out), .b(adder_2_cout), .out(adder_1_out), .cout(adder_1_cout));  // open: cin
  LED led_2 (.in(adder_1_cout));
  LED led_3 (.in(adder_2_out));
  not not_3 (not_3_out, in_3);
  Adder #(.width(1)) adder_2 (.a(not_2_out), .b(adder_3_cout), .out(adder_2_out), .cout(adder_2_cout));  // open: cin
  LED led_4 (.in(adder_3_out));
  Adder #(.width(1)) adder_3 (.a(not_3_out), .b(adder_4_cout), .out(adder_3_out), .cout(adder_3_cout));  // open: cin
  LED led_5 (.in(adder_4_out));
  not not_4 (not_4_out, in_4);
  Adder #(.width(1)) adder_4 (.a(not_4_out), .b(adder_5_cout), .out(adder_4_out), .cout(adder_4_cout));  // open: cin
  LED led_6 (.in(adder_5_out));
  not not_5 (not_5_out, in_5);
  Adder #(.width(1)) adder_5 (.a(not_5_out), .b(adder_6_cout), .out(adder_5_out), .cout(adder_5_cout));  // open: cin
  LED led_7 (.in(adder_6_out));
  not not_6 (not_6_out, in_6);
  Adder #(.width(1)) adder_6 (.a(not_6_out), .b(adder_7_cout), .out(adder_6_out), .cout(adder_6_cout));  // open: cin
  LED led_8 (.in(adder_7_out));
  not not_7 (not_7_out, in_7);
  not not_8 (not_8_out, in_8);
  Adder #(.width(1)) adder_7 (.a(not_7_out), .b(adder_8_cout), .out(adder_7_out), .cout(adder_7_cout));  // open: cin
  LED led_9 (.in(adder_8_out));
  Adder #(.width(1)) adder_8 (.a(not_8_out), .b(1'b1), .out(adder_8_out), .cout(adder_8_cout));  // open: cin
  LED led_10 (.in(adder_9_out));
  not not_9 (not_9_out, in_17);
  LED led_11 (.in(adder_9_cout));
  LED led_12 (.in(adder_10_out));
  not not_10 (not_10_out, in_18);
  Adder #(.width(1)) adder_9 (.a(not_9_out), .b(adder_10_cout), .out(adder_9_out), .cout(adder_9_cout));  // open: cin
  LED led_13 (.in(adder_11_out));
  not not_11 (not_11_out, in_19);
  Adder #(.width(1)) adder_10 (
    .a(not_10_out), .b(adder_11_cout), .out(adder_10_out), .cout(adder_10_cout));  // open: cin
  LED led_14 (.in(adder_12_out));
  not not_12 (not_12_out, in_20);
  Adder #(.width(1)) adder_11 (
    .a(not_11_out), .b(adder_12_cout), .out(adder_11_out), .cout(adder_11_cout));  // open: cin
  not not_13 (not_13_out, in_21);
  Adder #(.width(1)) adder_12 (
    .a(not_12_out), .b(adder_13_cout), .out(adder_12_out), .cout(adder_12_cout));  // open: cin
  LED led_15 (.in(adder_13_out));
  not not_14 (not_14_out, in_22);
  Adder #(.width(1)) adder_13 (
    .a(not_13_out), .b(adder_14_cout), .out(adder_13_out), .cout(adder_13_cout));  // open: cin
  LED led_16 (.in(adder_14_out));
  not not_15 (not_15_out, in_23);
  Adder #(.width(1)) adder_14 (
    .a(not_14_out), .b(adder_15_cout), .out(adder_14_out), .cout(adder_14_cout));  // open: cin
  LED led_17 (.in(adder_15_out));
  not not_16 (not_16_out, in_24);
  Adder #(.width(1)) adder_15 (
    .a(not_15_out), .b(adder_16_cout), .out(adder_15_out), .cout(adder_15_cout));  // open: cin
  LED led_18 (.in(adder_16_out));
  Adder #(.width(1)) adder_16 (
    .a(not_16_out), .b(adder_17_cout), .out(adder_16_out), .cout(adder_16_cout));  // open: cin
  LED led_19 (.in(adder_17_out));
  not not_17 (not_17_out, in_9);
  LED led_20 (.in(adder_18_out));
  not not_18 (not_18_out, in_10);
  Adder #(.width(1)) adder_17 (
    .a(not_17_out), .b(adder_18_cout), .out(adder_17_out), .cout(adder_17_cout));  // open: cin
  LED led_21 (.in(adder_19_out));
  not not_19 (not_19_out, in_11);
  Adder #(.width(1)) adder_18 (
    .a(not_18_out), .b(adder_19_cout), .out(adder_18_out), .cout(adder_18_cout));  // open: cin
  LED led_22 (.in(adder_20_out));
  not not_20 (not_20_out, in_12);
  Adder #(.width(1)) adder_19 (
    .a(not_19_out), .b(adder_20_cout), .out(adder_19_out), .cout(adder_19_cout));  // open: cin
  not not_21 (not_21_out, in_13);
  Adder #(.width(1)) adder_20 (
    .a(not_20_out), .b(adder_21_cout), .out(adder_20_out), .cout(adder_20_cout));  // open: cin
  LED led_23 (.in(adder_21_out));
  not not_22 (not_22_out, in_14);
  Adder #(.width(1)) adder_21 (
    .a(not_21_out), .b(adder_22_cout), .out(adder_21_out), .cout(adder_21_cout));  // open: cin
  LED led_24 (.in(adder_22_out));
  not not_23 (not_23_out, in_15);
  Adder #(.width(1)) adder_22 (
    .a(not_22_out), .b(adder_23_cout), .out(adder_22_out), .cout(adder_22_cout));  // open: cin
  LED led_25 (.in(adder_23_out));
  not not_24 (not_24_out, in_16);
  Adder #(.width(1)) adder_23 (
    .a(not_23_out), .b(adder_24_cout), .out(adder_23_out), .cout(adder_23_cout));  // open: cin
  LED led_26 (.in(adder_24_out));
  Adder #(.width(1)) adder_24 (.a(not_24_out), .b(1'b1), .out(adder_24_out), .cout(adder_24_cout));  // open: cin
endmodule
